# Fritzing sketch breadboard-design (saved by Fritzing 0.9.3b)
breadboards: 2

parts:
  U1 = ESP32S-HiLetgo [part_number=ESP32]
  LED1 = LED - 3mm [color="White (6500K)" package="3 mm [THT]"]
  R1 = Resistor [tolerance=±5% resistance=220 package="0402 [SMD]"]
  LED2 = LED - 3mm [color="Red (633nm)" package="3 mm [THT]"]
  LED3 = LED - 3mm [color="Yellow (592nm)" package="3 mm [THT]"]
  R2 = Resistor [tolerance=±5% resistance=220 package="0402 [SMD]"]
  R3 = Resistor [tolerance=±5% resistance=220 package="0402 [SMD]"]
  Smoke1 = mystery part, 2 pins [chip_label="Smoke Generator"]
  Q1 = MOSFET-NCHANNEL [part_number=2N7000 package=to-92]
  R4 = Resistor [tolerance=±5% resistance=470 package="0402 [SMD]"]

nets:
  N1: U1.GND, R1.Pin_1, R2.Pin_1, R3.Pin_1, Q1.S
  N2: U1.GPIO15, LED1.anode
  N3: U1.GPIO16, LED2.anode
  N4: U1.GPIO17, LED3.anode
  N5: U1.GPIO18, R4.Pin_0
  N6: LED1.cathode, R1.Pin_0
  N7: LED2.cathode, R2.Pin_0
  N8: LED3.cathode, R3.Pin_0
  12V: Smoke1.pin1
  N9: Smoke1.pin2, Q1.D
  N10: Q1.G, R4.Pin_1

custom parts:
  ESP32S-HiLetgo: HiLetgo ESP-WROOM-32 ESP32 ESP-32S Development Board 2.4GHz Dual-Mode WiFi + Bluetooth Dual Cores Microcontroller The ESP32 integrated with Antenna switches, RF Balun, power amplifiers, low-noise amplifiers, filters, and management modules, and the entire solution occupies the least area of PCB. 2.4 GHz Wi-Fi plus Bluetooth dual-mode chip, with TSMC Ultra-low power consumption 40nm technology,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
  MOSFET-NCHANNEL: Generic NMOS footprint
